# Fritzing sketch Braço_Robótico (saved by Fritzing 1.0.1rc)
breadboards: 2

parts:
  LM2596 = RioRand LM2596
  Bateria_litio_3_7v = LIPO-1000mAh [package=lipo-1000]
  ESP32_DEVKIT_V1 = DOIT Esp32 DevKit v1 (30 pins long, 11 pins width) [part_number=ESP32S-PIN30]
  SERVO_sg90 = Tower Pro SG90 servo [part_number=101246]
  SERVO2 = Tower Pro SG90 servo [part_number=101246]
  SERVO3 = Tower Pro SG90 servo [part_number=101246]
  SERVO4 = Tower Pro SG90 servo [part_number=101246]
  R1 = Resistor [tolerance=±5% resistance=220 package="0402 [SMD]"]
  R2 = Resistor [tolerance=±5% resistance=220 package="0402 [SMD]"]
  LED1 = smd LED [color="Red (635nm)" package="0805 [SMD]"]
  LED2 = smd LED [color="Green (555nm)" package="0805 [SMD]"]
  Buzzer_Ativo = Piezo Speaker
  U3 = LIPO-1000mAh [package=lipo-1000]

nets:
  N1: LM2596.Pin_1, Bateria_litio_3_7v.+, U3.+
  N2: LM2596.Pin_2, Bateria_litio_3_7v.-, U3.-
  +5V: LM2596.Pin_3, ESP32_DEVKIT_V1.VIN, SERVO_sg90.+5V, SERVO2.+5V, SERVO3.+5V, SERVO4.+5V
  N3: ESP32_DEVKIT_V1.3V3, R1.Pin_1, R2.Pin_1
  GND: ESP32_DEVKIT_V1.GND, SERVO_sg90.GND, SERVO2.GND, SERVO3.GND, SERVO4.GND, Buzzer_Ativo.pin1
  N4: ESP32_DEVKIT_V1.D14, LED2.anode
  N5: ESP32_DEVKIT_V1.D12, LED1.anode
  N6: ESP32_DEVKIT_V1.D13, Buzzer_Ativo.pin2
  N7: R1.Pin_0, LED2.cathode
  N8: R2.Pin_0, LED1.cathode

custom parts:
  DOIT Esp32 DevKit v1 (30 pins long, 11 pins width): The DOIT Esp32 DevKit v1 is one of the development board created by DOIT to evaluate the ESP-WROOM-32 module. It is based on the ESP32 microcontroller that boasts Wifi, Bluetooth, Ethernet and Low Power support all in a single chip. (vanepp) made breadboard work, adjusted pin numbering and labels and reduced size of schematic and cleaned up pcb. This chip is 30pins long (2 x15) and 11 pins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
  Tower Pro SG90 servo: Original file by John De Cristofaro http://www.adafruit.com/products/1449 Adafruit Feedback Servo (Small) Edited by: e-radionica.com 28/9/2015
