# Fritzing sketch Teste_Arduino_E220 (saved by Fritzing 1.0.1rc)
breadboards: 1

parts:
  Componente1 = Arduino Uno (Rev3) - ICSP
  Mod1 = ossoyoo-lora-module
  R1 = Resistor [tolerance=±5% resistance=4.7k package="0805 [SMD]"]
  R2 = Resistor [tolerance=±5% resistance=4.7k package="0805 [SMD]"]
  R3 = Resistor [tolerance=±5% resistance=4.7k package="0805 [SMD]"]

nets:
  N1: Componente1.D3_PWM, Mod1.AUX, R1.Pin_0
  N2: Componente1.D4, Mod1.TXD, R2.Pin_1
  N3: Componente1.D5_PWM, Mod1.RXD, R3.Pin_1
  N4: Componente1.D6_PWM, Mod1.M1
  N5: Componente1.D7, Mod1.M0
  N6: Componente1.3V3, R1.Pin_1, R2.Pin_0, R3.Pin_0
  5V: Componente1.5V, Mod1.VCC
  GND: Componente1.GND, Mod1.GND

custom parts:
  ossoyoo-lora-module: Osoyoo Long Distance wireless transceiver Uart LoRa Module.
