# Fritzing sketch teste_alcance (saved by Fritzing 1.0.1rc)

parts:
  A1 = FT232-AZ USB to TTL serial adapter
  Mod1 = ossoyoo-lora-module

nets:
  N1: A1.Pin_11, A1.Pin_23, Mod1.TXD
  N2: A1.Pin_12, A1.Pin_19, Mod1.RXD
  N3: A1.Pin_13, A1.Pin_16, A1.Pin_17, A1.Pin_22, Mod1.VCC
  N4: A1.Pin_15, A1.Pin_25, Mod1.GND

custom parts:
  FT232-AZ USB to TTL serial adapter: FT232-AZ USB to TTL serial adapter.
  ossoyoo-lora-module: Osoyoo Long Distance wireless transceiver Uart LoRa Module.
