# Fritzing sketch Carrinho_ControlePs4 (saved by Fritzing 1.0.1rc)
breadboards: 1

parts:
  M1 = DOIT Esp32 DevKit v1 (30 pins long, 11 pins width) [part_number=ESP32S-PIN30]
  S1 = H-Bridge with L298N
  M2 = gear-motor
  M3 = gear-motor
  VCC1 = Battery
  U1 = SWITCH-SPST-2 [package=switch-spst-vertical]

nets:
  GND: M1.GND, S1.GND, VCC1.-
  N1: M1.D32, S1.ENB
  N2: M1.D33, S1.IN4
  N3: M1.D25, S1.IN3
  N4: M1.D26, S1.IN2
  N5: M1.D27, S1.IN1
  N6: M1.D14, S1.ENA
  VIN: M1.VIN, S1.5V
  N7: S1.12V, U1.P
  N8: S1.M1-01, M3.pin_2
  N9: S1.M1-02, M3.pin_1
  N10: S1.M2-01, M2.pin_2
  N11: S1.M2-02, M2.pin_1
  N12: VCC1.+, U1.O

custom parts:
  DOIT Esp32 DevKit v1 (30 pins long, 11 pins width): The DOIT Esp32 DevKit v1 is one of the development board created by DOIT to evaluate the ESP-WROOM-32 module. It is based on the ESP32 microcontroller that boasts Wifi, Bluetooth, Ethernet and Low Power support all in a single chip. (vanepp) made breadboard work, adjusted pin numbering and labels and reduced size of schematic and cleaned up pcb. This chip is 30pins long (2 x15) and 11 pins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
  H-Bridge with L298N: h-bridge
  Battery: Your standard 2x 18650 battery pack (7.4 Volts)
